// Logisim project 3 alpha.circ as structural Verilog: 6 circuits, main circuit Main
module Main (
);

  wire ACC_read, ACC_write, alu_1_equal_flag, alu_1_greater_flag, alu_1_less_flag, alu_1_mux, ALU_activation,
       and_1_out, and_2_out, button_1_out, button_2_out, button_3_out, button_4_out, Clear_clock,
       control_unit_1_data_read, Counter_write, Equal_flag, GPU_add, GPU_select, GPU_subtract, Greater_flag,
       Halt, Keyboard_clear, Keyboard_read, Less_flag, MAR_write, not_1_out, not_2_out, R0_read, R0_write,
       R1_read, R1_write, R2_read, R2_write, R3_read, R3_write, R4_read, R4_write, R5_read, R5_write,
       RAM_read, RAM_write, register_1_q, Stack_read, Stack_write, Temp_read, Temp_write;
  wire [2:0] ALU_opcode, Clocks;
  wire [7:0] ACC, alu_1_result, Data_bus, gpu_1_output_0, gpu_1_output_1, gpu_1_output_2, gpu_1_output_3,
       gpu_1_output_4, gpu_1_output_5, gpu_1_output_6, gpu_1_output_7, gpu_1_output_8, gpu_1_output_9,
       gpu_1_output_10, gpu_1_output_11, gpu_1_output_12, gpu_1_output_13, gpu_1_output_14, gpu_1_output_15,
       gpu_1_output_16, gpu_1_output_17, gpu_1_output_18, gpu_1_output_19, keyboard_1_output, MAR_q,
       multiplexer_2_out, R0_q, R1_q, R2_q, R3_q, R4_q, R5_q, ram_1_data, Temp_q;
  wire [10:0] adder_1_out, control_unit_1_data, multiplexer_1_out, register_2_q, ROM_address, Stack_q;
  wire [10:8] Data_bus__wide;
  wire [15:0] Instruction_bus;

  DotMatrix #(.matrixcols(20), .matrixrows(8)) dotmatrix_1 (
    .col0(gpu_1_output_0), .col1(gpu_1_output_1), .col2(gpu_1_output_2), .col3(gpu_1_output_3),
    .col4(gpu_1_output_4), .col5(gpu_1_output_5), .col6(gpu_1_output_6), .col7(gpu_1_output_7),
    .col8(gpu_1_output_8), .col9(gpu_1_output_9), .col10(gpu_1_output_10), .col11(gpu_1_output_11),
    .col12(gpu_1_output_12), .col13(gpu_1_output_13), .col14(gpu_1_output_14), .col15(gpu_1_output_15),
    .col16(gpu_1_output_16), .col17(gpu_1_output_17), .col18(gpu_1_output_18), .col19(gpu_1_output_19));
  GPU gpu_1 (
    .Add(GPU_add), .Intput_data(Data_bus), .Select(GPU_select), .Subtract(GPU_subtract),
    .Output_0(gpu_1_output_0), .Output_2(gpu_1_output_2), .Output_3(gpu_1_output_3),
    .Output_4(gpu_1_output_4), .Output_5(gpu_1_output_5), .Output_6(gpu_1_output_6),
    .Output_7(gpu_1_output_7), .Output_8(gpu_1_output_8), .Output_9(gpu_1_output_9),
    .Output_10(gpu_1_output_10), .Output_11(gpu_1_output_11), .Output_12(gpu_1_output_12),
    .Output_13(gpu_1_output_13), .Output_14(gpu_1_output_14), .Output_15(gpu_1_output_15),
    .Output_16(gpu_1_output_16), .Output_17(gpu_1_output_17), .Output_18(gpu_1_output_18),
    .Output_19(gpu_1_output_19), .Output_1(gpu_1_output_1), .Data_clock(Clocks));
  Button button_1 (.out(button_1_out));
  Keyboard keyboard_1 (
    .Left(button_1_out), .Down(button_4_out), .Right(button_3_out), .Up(button_2_out),
    .Output(keyboard_1_output), .Key_clear(Keyboard_clear));
  Button button_2 (.out(button_2_out));
  Button button_3 (.out(button_3_out));
  Button button_4 (.out(button_4_out));
  assign Data_bus = Keyboard_read ? keyboard_1_output : 8'bz;  // Controlled_Buffer controlled_buffer_1
  Register #(.trigger("high")) MAR (.D(Data_bus), .Q(MAR_q), .clk(MAR_write));  // open: en, clr
  RAM ram_1 (.addr(MAR_q), .data(ram_1_data), .clk(RAM_write), .ld(RAM_read));  // open: sel, clr
  ROM #(.addrWidth(11), .dataWidth(16)) rom_1 (.addr(ROM_address), .data(Instruction_bus));  // open: sel
  not not_1 (not_1_out, RAM_read);
  assign ram_1_data = not_1_out ? Data_bus : 8'bz;  // Controlled_Buffer controlled_buffer_2
  assign Data_bus = RAM_read ? ram_1_data : 8'bz;  // Controlled_Buffer controlled_buffer_3
  Register #(.trigger("high")) R0 (.D(Data_bus), .Q(R0_q), .clk(R0_write));  // open: en, clr
  Register #(.trigger("high")) R1 (.D(Data_bus), .Q(R1_q), .clk(R1_write));  // open: en, clr
  Register #(.trigger("high")) R2 (.D(Data_bus), .Q(R2_q), .clk(R2_write));  // open: en, clr
  Register #(.trigger("high")) R3 (.D(Data_bus), .Q(R3_q), .clk(R3_write));  // open: en, clr
  Register #(.trigger("high")) R4 (.D(Data_bus), .Q(R4_q), .clk(R4_write));  // open: en, clr
  Register #(.trigger("high")) R5 (.D(Data_bus), .Q(R5_q), .clk(R5_write));  // open: en, clr
  Register #(.trigger("high")) u_ACC (.D(Data_bus), .Q(ACC), .clk(ACC_write));  // open: en, clr
  Pull_Resistor pull_resistor_1 (.node(Data_bus));
  assign Data_bus = R0_read ? R0_q : 8'bz;  // Controlled_Buffer controlled_buffer_4
  assign Data_bus = R1_read ? R1_q : 8'bz;  // Controlled_Buffer controlled_buffer_5
  assign Data_bus = R2_read ? R2_q : 8'bz;  // Controlled_Buffer controlled_buffer_6
  assign Data_bus = R3_read ? R3_q : 8'bz;  // Controlled_Buffer controlled_buffer_7
  assign Data_bus = R4_read ? R4_q : 8'bz;  // Controlled_Buffer controlled_buffer_8
  assign Data_bus = R5_read ? R5_q : 8'bz;  // Controlled_Buffer controlled_buffer_9
  assign Data_bus = ACC_read ? ACC : 8'bz;  // Controlled_Buffer controlled_buffer_10
  Control_unit control_unit_1 (
    .Write_clock(Clocks[2]), .R0_write(R0_write), .Data(control_unit_1_data), .R1_write(R1_write),
    .Instruction(Instruction_bus), .R2_write(R2_write), .R3_write(R3_write), .ACC_write(ACC_write),
    .Data_clock(Clocks[1]), .R0_read(R0_read), .R1_read(R1_read), .R2_read(R2_read), .R3_read(R3_read),
    .ACC_read(ACC_read), .Temp_write(Temp_write), .Temp_read(Temp_read), .Counter_enable(Counter_write),
    .Instruction_clock(Clocks[0]), .Stack_write(Stack_write), .Stack_read(Stack_read),
    .Data_read(control_unit_1_data_read), .ALU_opcode(ALU_opcode), .Greater_flag(Greater_flag),
    .Equal_flag(Equal_flag), .Less_flag(Less_flag), .ALU_activation(ALU_activation), .GPU_add(GPU_add),
    .MAR_write(MAR_write), .RAM_read(RAM_read), .RAM_write(RAM_write), .GPU_select(GPU_select),
    .R4_write(R4_write), .R5_write(R5_write), .R4_read(R4_read), .R5_read(R5_read),
    .Keyboard_read(Keyboard_read), .Keyboard_clear(Keyboard_clear), .GPU_subtruct(GPU_subtract), .Halt(Halt));
  assign {Data_bus__wide, Data_bus} = control_unit_1_data_read ? control_unit_1_data : 11'bz;  // Controlled_Buffer controlled_buffer_11
  not not_2 (not_2_out, register_1_q);
  Counter #(.width(11), .max('h7ff), .trigger("falling")) Program_counter (
    .load(register_1_q), .D(register_2_q), .count(not_2_out), .Q(ROM_address), .clk(and_1_out));  // open: carry, clr
  buf and_1 (and_1_out, Clocks[0]);  // AND_Gate AND_Gate
  Adder #(.width(11)) adder_1 (.a(ROM_address), .b({11{1'b0}}), .out(adder_1_out), .cin(1'b1));  // open: cout
  Multiplexer #(.width(11), .enable("true")) multiplexer_1 (
    .in0({Data_bus__wide, Data_bus}), .in1(Stack_q), .out(multiplexer_1_out), .sel(Stack_read));  // open: en
  Register #(.width(11), .trigger("high")) Stack (.D(adder_1_out), .Q(Stack_q), .clk(Stack_write));  // open: en, clr
  Register #(.width(1), .trigger("high")) register_1 (
    .D(Counter_write), .Q(register_1_q), .clk(Counter_write), .clr(Clear_clock));  // open: en
  Register #(.width(11), .trigger("high")) register_2 (
    .D(multiplexer_1_out), .Q(register_2_q), .clk(Counter_write));  // open: en, clr
  ALU alu_1 (
    .Operand_1(ACC), .Operand_2(Data_bus), .Result(alu_1_result), .Opcode(ALU_opcode),
    .Greater_flag(alu_1_greater_flag), .Equal_flag(alu_1_equal_flag), .Less_flag(alu_1_less_flag),
    .Mux(alu_1_mux));
  and and_2 (and_2_out, ALU_activation, Clocks[2]);
  Register #(.width(1), .trigger("high")) Greater (
    .D(alu_1_greater_flag), .Q(Greater_flag), .clk(and_2_out));  // open: en, clr
  Register #(.width(1), .trigger("high")) Equal (
    .D(alu_1_equal_flag), .Q(Equal_flag), .clk(and_2_out));  // open: en, clr
  Register #(.width(1), .trigger("high")) Less (.D(alu_1_less_flag), .Q(Less_flag), .clk(and_2_out));  // open: en, clr
  Multiplexer #(.width(8), .enable("true")) multiplexer_2 (
    .in0(Data_bus), .in1(alu_1_result), .out(multiplexer_2_out), .sel(alu_1_mux));  // open: en
  Register #(.trigger("high")) Temp (.D(multiplexer_2_out), .Q(Temp_q), .clk(Temp_write));  // open: en, clr
  assign Data_bus = Temp_read ? Temp_q : 8'bz;  // Controlled_Buffer controlled_buffer_12
  Clocks clocks_1 (
    .Write_clock(Clocks[2]), .Data_clock(Clocks[1]), .Instruction_clock(Clocks[0]), .Clear_clock(Clear_clock));
  // Probe on nothing

  // Other names for the same wires on the sheet: Instruction_clock = Clocks[0]; Data_clock = Clocks[1];
  //   Write_clock = Clocks[2]; Data_bus__wide[7:0] = Data_bus

  // Notes on the sheet:
  //   GPU
  //   Display
  //   Keyboard
  //   RAM
  //   ROM
  //   Registers
  //   Control Unit
  //   ALU
  //   Clock generator
endmodule

module Control_unit (
  input  Data_clock,
  input  Instruction_clock,
  input  Write_clock,
  input  Greater_flag,
  input  Equal_flag,
  input  Less_flag,
  input  [15:0] Instruction,
  output Counter_enable,
  output Data_read,
  output Temp_write,
  output Temp_read,
  output R0_write,
  output R1_write,
  output R2_write,
  output R3_write,
  output R4_write,
  output R5_write,
  output ACC_write,
  output R0_read,
  output R1_read,
  output R2_read,
  output R3_read,
  output R4_read,
  output R5_read,
  output ACC_read,
  output [10:0] Data,
  output Stack_write,
  output Stack_read,
  output [2:0] ALU_opcode,
  output ALU_activation,
  output MAR_write,
  output RAM_read,
  output RAM_write,
  output GPU_select,
  output GPU_add,
  output GPU_subtruct,
  output Keyboard_read,
  output Keyboard_clear,
  output Halt
);

  wire ADD, and_1_out, and_2_out, and_3_out, and_4_out, and_5_out, and_6_out, and_8_out, and_9_out,
       and_10_out, and_11_out, and_12_out, and_13_out, and_14_out, and_15_out, and_16_out, and_17_out,
       and_18_out, and_19_out, and_20_out, and_23_out, and_25_out, and_26_out, and_27_out, and_28_out,
       and_29_out, and_31_out, and_32_out, and_33_out, and_34_out, and_35_out, and_36_out, and_37_out,
       and_38_out, and_39_out, and_40_out, and_41_out, and_42_out, and_43_out, and_44_out, and_46_out,
       and_49_out, and_51_out, and_52_out, and_53_out, and_55_out, and_56_out, and_58_out, CAL, CMP, CPY,
       decoder_2_out7, GSEL, JE, JG, JL, JMP, KCL, KEY, LD, MAR, MR, MW, or_2_out, or_3_out, or_4_out,
       or_5_out, or_6_out, or_8_out, or_9_out, or_10_out, or_11_out, or_13_out, or_14_out, or_15_out,
       or_17_out, or_18_out, or_19_out, or_20_out, or_21_out, or_23_out, or_24_out, or_25_out, or_27_out,
       or_28_out, or_29_out, or_30_out, or_31_out, or_32_out, or_33_out, or_35_out, or_36_out, or_37_out,
       or_38_out, or_39_out, RET, Select_address, Select_data, SL, SR, SUB;
  wire [2:0] pull_resistor_3_node, pull_resistor_4_node;
  wire [7:0] multiplexer_1_out;
  wire [10:0] bit_extender_1_out;

  Decoder #(.select(5), .enable("true")) decoder_1 (
    .out1(LD), .out2(CPY), .out3(JMP), .out4(CAL), .out5(RET), .out6(CMP), .out7(ADD), .out8(SUB), .out9(JG),
    .out10(JE), .out11(JL), .out12(GPU_add), .out13(MAR), .out14(MR), .out15(MW), .out16(GSEL), .out17(SL),
    .out18(SR), .out19(KEY), .out20(KCL), .out21(GPU_subtruct), .out22(Halt), .sel(Instruction[15:11]));  // open: out0, out23, out24, out25, out26, out27, out28, out29, out30, out31, en
  Multiplexer #(.width(8), .enable("true")) multiplexer_1 (
    .in0(Instruction[7:0]), .in1(Instruction[10:3]), .out(multiplexer_1_out), .sel(Select_data));  // open: en
  assign bit_extender_1_out = {{3{1'b0}}, multiplexer_1_out};  // Bit_Extender bit_extender_1
  Pull_Resistor pull_resistor_1 (.node(Select_data));
  Multiplexer #(.width(11), .enable("true")) multiplexer_2 (
    .in0(bit_extender_1_out), .in1(Instruction[10:0]), .out(Data), .sel(Select_address));  // open: en
  and and_1 (and_1_out, LD, Instruction_clock, Data_clock);
  and and_2 (and_2_out, CPY, ~Instruction_clock, Data_clock);  // AND_Gate
  and and_3 (and_3_out, CPY, Instruction_clock, Data_clock);
  and and_4 (and_4_out, JMP, Instruction_clock, Data_clock);
  and and_5 (and_5_out, CAL, ~Instruction_clock, Data_clock);  // AND_Gate
  and and_6 (and_6_out, CAL, Instruction_clock, Data_clock);
  and and_7 (Stack_read, RET, Instruction_clock, Data_clock);
  and and_8 (and_8_out, JG, Instruction_clock, Data_clock, Greater_flag);
  and and_9 (and_9_out, JE, Instruction_clock, Data_clock, Equal_flag);
  and and_10 (and_10_out, JL, Instruction_clock, Data_clock, Less_flag);
  and and_11 (and_11_out, CMP, ~Instruction_clock, Data_clock);  // AND_Gate
  and and_12 (and_12_out, ADD, ~Instruction_clock, Data_clock);  // AND_Gate
  and and_13 (and_13_out, ADD, Instruction_clock, Data_clock);
  and and_14 (and_14_out, SUB, ~Instruction_clock, Data_clock);  // AND_Gate
  and and_15 (and_15_out, SUB, Instruction_clock, Data_clock);
  and and_16 (and_16_out, SL, ~Instruction_clock, Data_clock);  // AND_Gate
  and and_17 (and_17_out, SL, Instruction_clock, Data_clock);
  and and_18 (and_18_out, SR, ~Instruction_clock, Data_clock);  // AND_Gate
  and and_19 (and_19_out, SR, Instruction_clock, Data_clock);
  and and_20 (and_20_out, GSEL, Instruction_clock, Data_clock);
  and and_21 (Keyboard_read, KEY, Instruction_clock, Data_clock);
  and and_22 (Keyboard_clear, KCL, Instruction_clock, Data_clock);
  and and_23 (and_23_out, MAR, Instruction_clock, Data_clock);
  and and_24 (RAM_read, MR, ~Instruction_clock, Data_clock);  // AND_Gate
  and and_25 (and_25_out, MW, Instruction_clock, Data_clock);
  and and_26 (and_26_out, and_1_out, Write_clock);
  and and_27 (and_27_out, and_2_out, Write_clock);
  and and_28 (and_28_out, and_3_out, Write_clock);
  and and_29 (and_29_out, and_4_out, Write_clock);
  and and_30 (Stack_write, and_5_out, Write_clock);
  and and_31 (and_31_out, and_6_out, Write_clock);
  and and_32 (and_32_out, Stack_read, Write_clock);
  and and_33 (and_33_out, and_8_out, Write_clock);
  and and_34 (and_34_out, and_9_out, Write_clock);
  and and_35 (and_35_out, and_10_out, Write_clock);
  and and_36 (and_36_out, and_11_out, Write_clock);
  and and_37 (and_37_out, and_12_out, Write_clock);
  and and_38 (and_38_out, and_13_out, Write_clock);
  and and_39 (and_39_out, and_14_out, Write_clock);
  and and_40 (and_40_out, and_15_out, Write_clock);
  and and_41 (and_41_out, and_16_out, Write_clock);
  and and_42 (and_42_out, and_17_out, Write_clock);
  and and_43 (and_43_out, and_18_out, Write_clock);
  and and_44 (and_44_out, and_19_out, Write_clock);
  and and_45 (GPU_select, and_20_out, Write_clock);
  and and_46 (and_46_out, Keyboard_read, Write_clock);
  // AND_Gate and_47 has open pins: in1=Keyboard_clear, in3=Write_clock, out=open
  and and_48 (MAR_write, and_23_out, Write_clock);
  and and_49 (and_49_out, RAM_read, Write_clock);
  and and_50 (RAM_write, and_25_out, Write_clock);
  assign ALU_opcode = and_11_out ? 3'b011 : 3'bz;  // Controlled_Buffer controlled_buffer_1
  assign ALU_opcode = and_12_out ? 3'b001 : 3'bz;  // Controlled_Buffer controlled_buffer_2
  assign ALU_opcode = and_14_out ? 3'b010 : 3'bz;  // Controlled_Buffer controlled_buffer_3
  assign ALU_opcode = and_16_out ? 3'b100 : 3'bz;  // Controlled_Buffer controlled_buffer_4
  or or_1 (Data_read, and_1_out, or_2_out);
  or or_2 (or_2_out, and_4_out, or_3_out);
  assign ALU_opcode = and_18_out ? 3'b101 : 3'bz;  // Controlled_Buffer controlled_buffer_5
  or or_3 (or_3_out, and_6_out, or_4_out);
  or or_4 (or_4_out, and_8_out, or_5_out);
  or or_5 (or_5_out, and_9_out, and_10_out);
  Pull_Resistor pull_resistor_2 (.node(ALU_opcode));
  or or_6 (or_6_out, and_20_out, GPU_add, GPU_subtruct);
  or or_7 (Select_address, and_4_out, or_8_out);
  or or_8 (or_8_out, and_6_out, or_9_out);
  or or_9 (or_9_out, and_8_out, or_10_out);
  or or_10 (or_10_out, and_9_out, and_10_out);
  or or_11 (or_11_out, and_11_out, and_12_out, and_14_out);
  or or_12 (ALU_activation, and_36_out, or_13_out);
  or or_13 (or_13_out, and_12_out, or_14_out);
  or or_14 (or_14_out, and_14_out, or_15_out);
  or or_15 (or_15_out, and_16_out, and_18_out);
  // AND_Gate and_51 has open pins: out=and_51_out
  or or_16 (Counter_enable, and_29_out, or_17_out);
  or or_17 (or_17_out, and_31_out, or_18_out);
  or or_18 (or_18_out, and_32_out, or_19_out);
  or or_19 (or_19_out, and_33_out, or_20_out);
  or or_20 (or_20_out, and_34_out, and_35_out);
  buf and_52 (and_52_out, and_53_out);  // AND_Gate
  buf and_53 (and_53_out, and_51_out);  // AND_Gate
  // AND_Gate and_54 has open pins: in1=and_52_out, out=open
  Pull_Resistor pull_resistor_3 (.node(pull_resistor_3_node));
  or or_21 (or_21_out, and_26_out, or_35_out);
  assign pull_resistor_3_node = or_21_out ? Instruction[10:8] : 3'bz;  // Controlled_Buffer controlled_buffer_6
  Decoder #(.select(3), .disabled(0), .enable("true")) decoder_2 (
    .out0(R0_write), .out1(R1_write), .out2(R2_write), .out3(R3_write), .out4(R4_write), .out5(R5_write),
    .out7(decoder_2_out7), .sel(pull_resistor_3_node), .en(or_30_out));  // open: out6
  assign pull_resistor_3_node = and_28_out ? Instruction[7:5] : 3'bz;  // Controlled_Buffer controlled_buffer_7
  or or_22 (Temp_write, and_27_out, or_23_out);
  or or_23 (or_23_out, and_37_out, or_24_out);
  or or_24 (or_24_out, and_39_out, or_25_out);
  or or_25 (or_25_out, and_41_out, and_43_out);
  or or_26 (Temp_read, and_3_out, or_27_out);
  or or_27 (or_27_out, and_13_out, or_28_out);
  or or_28 (or_28_out, and_15_out, or_29_out);
  or or_29 (or_29_out, and_17_out, and_19_out);
  or or_30 (or_30_out, or_21_out, and_28_out);
  or or_31 (or_31_out, and_38_out, or_32_out);
  or or_32 (or_32_out, and_40_out, or_33_out);
  or or_33 (or_33_out, and_42_out, and_44_out);
  or or_34 (ACC_write, decoder_2_out7, or_31_out);
  or or_35 (or_35_out, and_46_out, and_49_out);
  or or_36 (or_36_out, and_2_out, or_37_out);
  or or_37 (or_37_out, or_11_out, or_38_out);
  or or_38 (or_38_out, or_6_out, or_39_out);
  or or_39 (or_39_out, and_23_out, and_25_out);
  Pull_Resistor pull_resistor_4 (.node(pull_resistor_4_node));
  assign pull_resistor_4_node = or_36_out ? Instruction[10:8] : 3'bz;  // Controlled_Buffer controlled_buffer_8
  Decoder #(.select(3), .disabled(0), .enable("true")) decoder_3 (
    .out0(R0_read), .out1(R1_read), .out2(R2_read), .out3(R3_read), .out4(R4_read), .out5(R5_read),
    .out7(ACC_read), .sel(pull_resistor_4_node), .en(or_36_out));  // open: out6
  buf and_55 (and_55_out, and_56_out);  // AND_Gate
  // AND_Gate and_56 has open pins: out=and_56_out
  // AND_Gate and_57 has open pins: in1=and_58_out, out=open
  buf and_58 (and_58_out, and_55_out);  // AND_Gate

  // Other names for the same wires on the sheet: Counter_write = Counter_enable; Address[10:0] = Instruction[10:0];
  //   Data_2[7:0] = Instruction[7:0]; Data_t[7:0] = Instruction[10:3]; GADD = GPU_add; GSUB = GPU_subtruct;
  //   Opcode[4:0] = Instruction[15:11]; Register_1[2:0] = Instruction[10:8]; Register_2[2:0] = Instruction[7:5]

  // Notes on the sheet:
  //   LD
  //   CPY
  //   JMP
  //   CAL
  //   RET
  //   JG
  //   JE
  //   JL
  //   CMP
  //   ADD
  //   SUB
  //   SL
  //   SR
  //   GSEL
  //   GADD
  //   GSUB
  //   KEY
  //   KCL
  //   HALT
  //   MAR
  //   MR
  //   MW
endmodule

module Clocks (
  output Write_clock,
  output Data_clock,
  output Instruction_clock,
  output Clear_clock
);

  wire Base, Old_read, Old_write;

  Clock clock_1 (.out(Base));
  Counter #(.width(1), .max('h1), .trigger("falling")) counter_1 (
    .Q(Old_read), .clk(Base));  // open: load, D, count, carry, clr
  Counter #(.width(2), .max('h1)) counter_2 (.carry(Old_write), .clk(Base));  // open: load, D, count, Q, clr
  and and_1 (Write_clock, ~Base, Old_write, Old_read, Data_clock);  // AND_Gate
  Counter #(.width(1), .max('h1), .trigger("falling")) counter_3 (
    .Q(Instruction_clock), .clk(Old_read));  // open: load, D, count, carry, clr
  or or_1 (Data_clock, Old_write, Old_read);
  and and_2 (Clear_clock, Base, Old_write, ~Old_read, ~Instruction_clock);  // AND_Gate

  // Other names for the same wires on the sheet: Instruction = Instruction_clock
endmodule

module ALU (
  input  [7:0] Operand_1,
  input  [7:0] Operand_2,
  input  [2:0] Opcode,
  output Mux,
  output [7:0] Result,
  output Greater_flag,
  output Equal_flag,
  output Less_flag
);

  wire comparator_1_eq, comparator_1_gt, comparator_1_lt, decoder_1_out1, decoder_1_out2, decoder_1_out3,
       decoder_1_out4, decoder_1_out5;
  wire [7:0] adder_1_out, shifter_1_out, shifter_2_out, subtractor_1_out;

  Pull_Resistor pull_resistor_1 (.node(Operand_2));
  Pull_Resistor pull_resistor_2 (.node(Operand_1));
  Adder adder_1 (.a(Operand_1), .b(Operand_2), .out(adder_1_out));  // open: cin, cout
  Subtractor subtractor_1 (.a(Operand_1), .b(Operand_2), .out(subtractor_1_out));  // open: bin, bout
  Shifter shifter_1 (.in(Operand_1), .\dist (3'b001), .out(shifter_1_out));
  Shifter #(.shift("lr")) shifter_2 (.in(Operand_1), .\dist (3'b001), .out(shifter_2_out));
  Comparator #(.mode("unsigned")) comparator_1 (
    .a(Operand_1), .b(Operand_2), .gt(comparator_1_gt), .eq(comparator_1_eq), .lt(comparator_1_lt));
  Decoder #(.select(3), .enable("true")) decoder_1 (
    .out1(decoder_1_out1), .out2(decoder_1_out2), .out3(decoder_1_out3), .out4(decoder_1_out4),
    .out5(decoder_1_out5), .sel(Opcode));  // open: out0, out6, out7, en
  Pull_Resistor pull_resistor_3 (.node(Opcode));
  Pull_Resistor pull_resistor_4 (.node(decoder_1_out2));
  Pull_Resistor pull_resistor_5 (.node(decoder_1_out1));
  assign Result = decoder_1_out2 ? subtractor_1_out : 8'bz;  // Controlled_Buffer controlled_buffer_1
  Pull_Resistor pull_resistor_6 (.node(decoder_1_out3));
  Pull_Resistor pull_resistor_7 (.node(decoder_1_out5));
  Pull_Resistor pull_resistor_8 (.node(decoder_1_out4));
  assign Result = decoder_1_out1 ? adder_1_out : 8'bz;  // Controlled_Buffer controlled_buffer_2
  assign Result = decoder_1_out4 ? shifter_1_out : 8'bz;  // Controlled_Buffer controlled_buffer_3
  assign Result = decoder_1_out5 ? shifter_2_out : 8'bz;  // Controlled_Buffer controlled_buffer_4
  Pull_Resistor pull_resistor_9 (.node(Result));
  or or_1 (Mux, decoder_1_out1, decoder_1_out2, decoder_1_out4, decoder_1_out5);
  Pull_Resistor pull_resistor_10 (.node(Mux));
  assign Greater_flag = decoder_1_out3 ? comparator_1_gt : 1'bz;  // Controlled_Buffer controlled_buffer_5
  assign Equal_flag = decoder_1_out3 ? comparator_1_eq : 1'bz;  // Controlled_Buffer controlled_buffer_6
  assign Less_flag = decoder_1_out3 ? comparator_1_lt : 1'bz;  // Controlled_Buffer controlled_buffer_7
  Pull_Resistor pull_resistor_11 (.node(Less_flag));
  Pull_Resistor pull_resistor_12 (.node(Greater_flag));
  Pull_Resistor pull_resistor_13 (.node(Equal_flag));
endmodule

module GPU (
  input  Select,
  input  Add,
  input  Subtract,
  input  [2:0] Data_clock,
  input  [7:0] Intput_data,
  output [7:0] Output_0,
  output [7:0] Output_5,
  output [7:0] Output_10,
  output [7:0] Output_15,
  output [7:0] Output_1,
  output [7:0] Output_6,
  output [7:0] Output_11,
  output [7:0] Output_16,
  output [7:0] Output_2,
  output [7:0] Output_7,
  output [7:0] Output_12,
  output [7:0] Output_17,
  output [7:0] Output_3,
  output [7:0] Output_8,
  output [7:0] Output_13,
  output [7:0] Output_18,
  output [7:0] Output_4,
  output [7:0] Output_9,
  output [7:0] Output_14,
  output [7:0] Output_19
);

  wire _0, _1, _2, _3, _4, _5, _6, _7, _8, _9, _10, _11, _12, _13, _14, _15, _16, _17, _18, _19, and_1_out,
       and_2_out, and_3_out, and_4_out, and_5_out, and_6_out, and_7_out, and_8_out, and_9_out, and_10_out,
       and_11_out, and_12_out, and_13_out, and_14_out, and_15_out, and_16_out, and_17_out, and_18_out,
       and_19_out, and_20_out, and_21_out, and_22_out, and_23_out, and_24_out, and_25_out, and_26_out,
       and_27_out, and_28_out, and_29_out, and_30_out, and_31_out, and_32_out, and_33_out, and_34_out,
       and_35_out, and_36_out, and_37_out, and_38_out, and_39_out, and_40_out, and_41_out, and_42_out,
       and_43_out, and_44_out, and_45_out, and_46_out, and_47_out, and_48_out, or_1_out, or_4_out, or_5_out,
       Read, Write;
  wire [4:0] register_1_q;
  wire [7:0] adder_1_out, controlled_buffer_2_out, Local_bus, subtractor_1_out, Temp_q;

  Register #(.width(5), .trigger("high")) register_1 (
    .D(Local_bus[4:0]), .Q(register_1_q), .clk(Select));  // open: en, clr
  and and_1 (and_1_out, Add, Data_clock[1], ~Data_clock[0]);  // AND_Gate
  and and_2 (and_2_out, Add, Data_clock[1], Data_clock[0]);
  and and_3 (and_3_out, Subtract, Data_clock[1], ~Data_clock[0]);  // AND_Gate
  and and_4 (and_4_out, Subtract, Data_clock[1], Data_clock[0]);
  and and_5 (and_5_out, and_1_out, Data_clock[2]);
  and and_6 (and_6_out, and_2_out, Data_clock[2]);
  and and_7 (and_7_out, and_3_out, Data_clock[2]);
  and and_8 (and_8_out, and_4_out, Data_clock[2]);
  Decoder #(.select(5), .disabled(0), .enable("true")) decoder_1 (
    .out0(_0), .out1(_1), .out2(_2), .out3(_3), .out4(_4), .out5(_5), .out6(_6), .out7(_7), .out8(_8),
    .out9(_9), .out10(_10), .out11(_11), .out12(_12), .out13(_13), .out14(_14), .out15(_15), .out16(_16),
    .out17(_17), .out18(_18), .out19(_19), .sel(register_1_q), .en(or_1_out));  // open: out20, out21, out22, out23, out24, out25, out26, out27, out28, out29, out30, out31
  or or_1 (or_1_out, and_1_out, and_6_out, and_3_out, and_8_out);
  or or_2 (Read, and_1_out, and_3_out);
  or or_3 (Write, and_6_out, and_8_out);
  Pull_Resistor pull_resistor_1 (.node(Select));
  or or_4 (or_4_out, and_5_out, and_7_out);
  Pull_Resistor pull_resistor_2 (.node(Add));
  assign Local_bus = Select ? Intput_data : 8'bz;  // Controlled_Buffer controlled_buffer_1
  Pull_Resistor pull_resistor_3 (.node(Subtract));
  Pull_Resistor pull_resistor_4 (.node(Intput_data));
  Pull_Resistor pull_resistor_5 (.node(Local_bus));
  Adder adder_1 (.a(Local_bus), .b(Intput_data), .out(adder_1_out));  // open: cin, cout
  Subtractor subtractor_1 (.a(Local_bus), .b(Intput_data), .out(subtractor_1_out));  // open: bin, bout
  or or_5 (or_5_out, and_2_out, and_4_out);
  assign controlled_buffer_2_out = and_1_out ? adder_1_out : 8'bz;  // Controlled_Buffer controlled_buffer_2
  assign controlled_buffer_2_out = and_3_out ? subtractor_1_out : 8'bz;  // Controlled_Buffer controlled_buffer_3
  Pull_Resistor pull_resistor_6 (.node(Data_clock));
  assign Local_bus = or_5_out ? Temp_q : 8'bz;  // Controlled_Buffer controlled_buffer_4
  Register #(.trigger("high")) Temp (.D(controlled_buffer_2_out), .Q(Temp_q), .clk(or_4_out));  // open: en, clr
  Register #(.trigger("high")) register_2 (.D(Local_bus), .Q(Output_0), .clk(and_9_out));  // open: en, clr
  and and_9 (and_9_out, _0, Write);
  and and_10 (and_10_out, _0, Read);
  assign Local_bus = and_10_out ? Output_0 : 8'bz;  // Controlled_Buffer controlled_buffer_5
  Register #(.trigger("high")) register_3 (.D(Local_bus), .Q(Output_1), .clk(and_11_out));  // open: en, clr
  and and_11 (and_11_out, _1, Write);
  and and_12 (and_12_out, _1, Read);
  assign Local_bus = and_12_out ? Output_1 : 8'bz;  // Controlled_Buffer controlled_buffer_6
  Register #(.trigger("high")) register_4 (.D(Local_bus), .Q(Output_2), .clk(and_13_out));  // open: en, clr
  and and_13 (and_13_out, _2, Write);
  and and_14 (and_14_out, _2, Read);
  assign Local_bus = and_14_out ? Output_2 : 8'bz;  // Controlled_Buffer controlled_buffer_7
  Register #(.trigger("high")) register_5 (.D(Local_bus), .Q(Output_3), .clk(and_15_out));  // open: en, clr
  and and_15 (and_15_out, _3, Write);
  and and_16 (and_16_out, _3, Read);
  assign Local_bus = and_16_out ? Output_3 : 8'bz;  // Controlled_Buffer controlled_buffer_8
  Register #(.trigger("high")) register_6 (.D(Local_bus), .Q(Output_4), .clk(and_17_out));  // open: en, clr
  and and_17 (and_17_out, _4, Write);
  and and_18 (and_18_out, _4, Read);
  assign Local_bus = and_18_out ? Output_4 : 8'bz;  // Controlled_Buffer controlled_buffer_9
  Register #(.trigger("high")) register_7 (.D(Local_bus), .Q(Output_5), .clk(and_19_out));  // open: en, clr
  and and_19 (and_19_out, _5, Write);
  and and_20 (and_20_out, _5, Read);
  Register #(.trigger("high")) register_8 (.D(Local_bus), .Q(Output_6), .clk(and_21_out));  // open: en, clr
  and and_21 (and_21_out, _6, Write);
  and and_22 (and_22_out, _6, Read);
  Register #(.trigger("high")) register_9 (.D(Local_bus), .Q(Output_7), .clk(and_23_out));  // open: en, clr
  and and_23 (and_23_out, _7, Write);
  and and_24 (and_24_out, _7, Read);
  Register #(.trigger("high")) register_10 (.D(Local_bus), .Q(Output_8), .clk(and_25_out));  // open: en, clr
  and and_25 (and_25_out, _8, Write);
  and and_26 (and_26_out, _8, Read);
  Register #(.trigger("high")) register_11 (.D(Local_bus), .Q(Output_9), .clk(and_27_out));  // open: en, clr
  and and_27 (and_27_out, _9, Write);
  and and_28 (and_28_out, _9, Read);
  assign Local_bus = and_20_out ? Output_5 : 8'bz;  // Controlled_Buffer controlled_buffer_10
  assign Local_bus = and_22_out ? Output_6 : 8'bz;  // Controlled_Buffer controlled_buffer_11
  assign Local_bus = and_24_out ? Output_7 : 8'bz;  // Controlled_Buffer controlled_buffer_12
  assign Local_bus = and_26_out ? Output_8 : 8'bz;  // Controlled_Buffer controlled_buffer_13
  assign Local_bus = and_28_out ? Output_9 : 8'bz;  // Controlled_Buffer controlled_buffer_14
  and and_29 (and_29_out, _10, Write);
  and and_30 (and_30_out, _10, Read);
  and and_31 (and_31_out, _11, Write);
  and and_32 (and_32_out, _11, Read);
  and and_33 (and_33_out, _12, Write);
  and and_34 (and_34_out, _12, Read);
  and and_35 (and_35_out, _13, Write);
  and and_36 (and_36_out, _13, Read);
  and and_37 (and_37_out, _14, Write);
  and and_38 (and_38_out, _14, Read);
  Register #(.trigger("high")) register_12 (.D(Local_bus), .Q(Output_10), .clk(and_29_out));  // open: en, clr
  assign Local_bus = and_30_out ? Output_10 : 8'bz;  // Controlled_Buffer controlled_buffer_15
  Register #(.trigger("high")) register_13 (.D(Local_bus), .Q(Output_11), .clk(and_31_out));  // open: en, clr
  assign Local_bus = and_32_out ? Output_11 : 8'bz;  // Controlled_Buffer controlled_buffer_16
  Register #(.trigger("high")) register_14 (.D(Local_bus), .Q(Output_12), .clk(and_33_out));  // open: en, clr
  assign Local_bus = and_34_out ? Output_12 : 8'bz;  // Controlled_Buffer controlled_buffer_17
  Register #(.trigger("high")) register_15 (.D(Local_bus), .Q(Output_13), .clk(and_35_out));  // open: en, clr
  assign Local_bus = and_36_out ? Output_13 : 8'bz;  // Controlled_Buffer controlled_buffer_18
  Register #(.trigger("high")) register_16 (.D(Local_bus), .Q(Output_14), .clk(and_37_out));  // open: en, clr
  assign Local_bus = and_38_out ? Output_14 : 8'bz;  // Controlled_Buffer controlled_buffer_19
  Register #(.trigger("high")) register_17 (.D(Local_bus), .Q(Output_15), .clk(and_39_out));  // open: en, clr
  and and_39 (and_39_out, _15, Write);
  and and_40 (and_40_out, _15, Read);
  Register #(.trigger("high")) register_18 (.D(Local_bus), .Q(Output_16), .clk(and_41_out));  // open: en, clr
  and and_41 (and_41_out, _16, Write);
  and and_42 (and_42_out, _16, Read);
  Register #(.trigger("high")) register_19 (.D(Local_bus), .Q(Output_17), .clk(and_43_out));  // open: en, clr
  and and_43 (and_43_out, _17, Write);
  and and_44 (and_44_out, _17, Read);
  Register #(.trigger("high")) register_20 (.D(Local_bus), .Q(Output_18), .clk(and_45_out));  // open: en, clr
  and and_45 (and_45_out, _18, Write);
  and and_46 (and_46_out, _18, Read);
  Register #(.trigger("high")) register_21 (.D(Local_bus), .Q(Output_19), .clk(and_47_out));  // open: en, clr
  and and_47 (and_47_out, _19, Write);
  and and_48 (and_48_out, _19, Read);
  Pull_Resistor pull_resistor_7 (.node(Output_15));
  assign Local_bus = and_40_out ? Output_15 : 8'bz;  // Controlled_Buffer controlled_buffer_20
  assign Local_bus = and_42_out ? Output_16 : 8'bz;  // Controlled_Buffer controlled_buffer_21
  assign Local_bus = and_44_out ? Output_17 : 8'bz;  // Controlled_Buffer controlled_buffer_22
  assign Local_bus = and_46_out ? Output_18 : 8'bz;  // Controlled_Buffer controlled_buffer_23
  assign Local_bus = and_48_out ? Output_19 : 8'bz;  // Controlled_Buffer controlled_buffer_24

  // Other names for the same wires on the sheet: Instruction_clock = Data_clock[0]; Data_clock_t = Data_clock[1];
  //   Write_clock = Data_clock[2]
endmodule

module Keyboard (
  input  Left,
  input  Down,
  input  Right,
  input  Up,
  input  Key_clear,
  output [7:0] Output
);

  wire and_1_out, and_2_out, and_3_out, and_4_out, and_5_out, Key_press, register_1_q;
  wire [2:0] controlled_buffer_1_out, register_2_q;

  and and_1 (and_1_out, Left, ~Down, ~Right, ~Up);  // AND_Gate
  assign controlled_buffer_1_out = and_1_out ? 3'b001 : 3'bz;  // Controlled_Buffer controlled_buffer_1
  Pull_Resistor pull_resistor_1 (.node(Left));
  and and_2 (and_2_out, Down, ~Left, ~Right, ~Up);  // AND_Gate
  assign controlled_buffer_1_out = and_2_out ? 3'b010 : 3'bz;  // Controlled_Buffer controlled_buffer_2
  Pull_Resistor pull_resistor_2 (.node(Down));
  and and_3 (and_3_out, Right, ~Left, ~Down, ~Up);  // AND_Gate
  assign controlled_buffer_1_out = and_3_out ? 3'b011 : 3'bz;  // Controlled_Buffer controlled_buffer_3
  Pull_Resistor pull_resistor_3 (.node(Up));
  Pull_Resistor pull_resistor_4 (.node(Right));
  and and_4 (and_4_out, Up, ~Left, ~Down, ~Right);  // AND_Gate
  assign controlled_buffer_1_out = and_4_out ? 3'b100 : 3'bz;  // Controlled_Buffer controlled_buffer_4
  Pull_Resistor pull_resistor_5 (.node(controlled_buffer_1_out));
  Register #(.width(1)) register_1 (.D(Key_press), .Q(register_1_q), .clk(Key_press), .clr(Key_clear));  // open: en
  Register #(.width(3), .trigger("high")) register_2 (
    .D(controlled_buffer_1_out), .Q(register_2_q), .clk(and_5_out), .clr(Key_clear));  // open: en
  buf and_5 (and_5_out, Key_press);  // AND_Gate AND_Gate
  Pull_Resistor pull_resistor_6 (.node(Key_clear));
  assign Output = {{5{1'b0}}, register_2_q};  // Bit_Extender bit_extender_1
  or or_1 (Key_press, Left, Down, Right, Up);

  // Other names for the same wires on the sheet: Clear = Key_clear
endmodule
